# Fritzing sketch soundbox (saved by Fritzing 0.5.2b)
breadboards: 2

parts:
  U1 = atmega168
  Programming_header = mystery part, 6 pins [chip_label=ICSP spacing=100mil]
  R1 = Resistor [resistance=1k package=THT]
  R1_2 = Resistor [resistance=1k package=THT]
  J1 = Piezo Speaker
  R2 = Resistor [resistance=220 package=THT]
  R3 = Resistor [resistance=220 package=THT]
  LED2 = green LED - 5mm [package="5 mm [THT]"]
  LED1 = green LED - 5mm [package="5 mm [THT]"]
  XTAL1 = Crystal [package=THT]
  R4 = Rotary Potentiometer (Large) [package=THT]
  R5 = Rotary Potentiometer (Large) [package=THT]
  C8 = Ceramic Capacitor [capacitance=100nF rated_voltage=35V package="200 mil [THT, multilayer]"]
  S1 = Pushbutton [package="[THT]"]
  C6 = Ceramic Capacitor [capacitance=100nF rated_voltage=35V package="200 mil [THT, multilayer]"]
  C6_2 = Ceramic Capacitor [capacitance=100nF rated_voltage=35V package="200 mil [THT, multilayer]"]
  C5 = Ceramic Capacitor [capacitance=100nF rated_voltage=35V package="200 mil [THT, multilayer]"]
  C4 = Ceramic Capacitor [capacitance=100nF rated_voltage=35V package="200 mil [THT, multilayer]"]
  C7 = Ceramic Capacitor [capacitance=100nF rated_voltage=35V package="200 mil [THT, multilayer]"]

nets:
  N1: U1.connector0, Programming_header.pin3
  N2: U1.connector1, S1.Pin_3, S1.Pin_4
  N3: U1.connector8, XTAL1.pin_0, C6.1
  N4: U1.connector9, XTAL1.pin_1, C6_2.0
  N5: U1.connector11, R1.Pin_0
  N6: U1.connector14, R3.Pin_0
  N7: U1.connector16, Programming_header.pin5
  N8: U1.connector17, Programming_header.pin1
  N9: U1.connector18, Programming_header.pin2
  N10: U1.connector19, U1.connector20, Programming_header.pin6, R2.Pin_0, R4.leg1, R5.leg1, C8.1, C7.0
  GND: U1.connector21, Programming_header.pin4, J1.pin1, LED2.cathode, LED1.cathode, R4.leg2, R5.leg2, C8.0, S1.Pin_1, S1.Pin_2, C6.0, C6_2.1, C5.0, C4.0, C7.1
  N11: U1.connector22, R4.wiper
  N12: U1.connector23, R5.wiper
  N13: R1.Pin_1, R1_2.Pin_0, C4.1
  N14: R1_2.Pin_1, J1.pin2, C5.1
  N15: R2.Pin_1, LED1.anode
  N16: R3.Pin_1, LED2.anode
